# Fritzing sketch rpi-leds-and-screen (saved by Fritzing 0.9.4)
circuit board: 8.46667cm x 5.64444cm
perfboards: 1

parts:
  Q1 = MOSFET-NCHANNEL [package=to-92]
  R1 = Resistor [tolerance=±5% resistance=5.1k package=THT]
  R2 = Resistor [tolerance=±5% resistance=5.1k package=THT]
  Raspberry_Pi_1 = Raspberry Pi 3 [part_number=RPI-3-V1.2]
  Part1 = ws2812b [package="smd 2812b"]
  SSD1331 = SSD1331 96x64 OLED
  Rotary_Encoder = Rotary Encoder

nets:
  N1: Q1.D, R2.Pin_1, Part1.DIN
  N2: Q1.S, R1.Pin_1, Raspberry_Pi_1.GIPO18
  3V3: Q1.G, R1.Pin_0, Raspberry_Pi_1.3v3, Raspberry_Pi_1.3V3, SSD1331.VCC, Rotary_Encoder.+
  5V: R2.Pin_0, Raspberry_Pi_1.5V, Part1.VDD
  GND: Raspberry_Pi_1.GND, Part1.VSS, SSD1331.GND, Rotary_Encoder.GND
  N3: Raspberry_Pi_1.GIPO10, SSD1331.SDA
  N4: Raspberry_Pi_1.GIPO11, SSD1331.SCL
  N5: Raspberry_Pi_1.GIPO5, Rotary_Encoder.CLK
  N6: Raspberry_Pi_1.GIPO6, Rotary_Encoder.DT
  N7: Raspberry_Pi_1.GIPO13, Rotary_Encoder.SW
  N8: Raspberry_Pi_1.GIPO8, SSD1331.RC
  N9: Raspberry_Pi_1.GIPO25, SSD1331.RES
  N10: Raspberry_Pi_1.GIPO24, SSD1331.DC

notes:
  DEFG
  HIJK
  LMNO
  PQRS
  TUVW

custom parts:
  Rotary Encoder: Rotary Encoder from Keyes
